# Fritzing sketch schematic (saved by Fritzing 0.9.3b)
breadboards: 1

parts:
  940nm_LED_-_V(F)_1_5;_I(F)_100mA = LED - 5mm [color="Red (633nm)" package="5 mm [THT]"]
  R1_-_10ohm = Resistor [tolerance=±5% resistance=220 package=THT]
  2_5V_DC = DC Power [voltage=5]

nets:
  N1: 940nm_LED_-_V(F)_1_5;_I(F)_100mA.cathode, 2_5V_DC.V+
  N2: 940nm_LED_-_V(F)_1_5;_I(F)_100mA.anode, R1_-_10ohm.Pin_0
  N3: R1_-_10ohm.Pin_1, 2_5V_DC.V-
